// Logisim project Turing.circ as structural Verilog: 8 circuits, main circuit main
module main (
);

  wire addrdec_1_count, addrdec_1_in_out, addrdec_1_reg0, addrdec_1_reg1, addrdec_1_reg2, addrdec_1_reg3,
       addrdec_1_reg4, addrdec_1_reg5, addrdec_1_stack, addrdec_2_count, addrdec_2_in_out, addrdec_2_reg0,
       addrdec_2_reg1, addrdec_2_reg2, addrdec_2_reg3, addrdec_2_reg4, addrdec_2_reg5, addrdec_2_stack,
       addrdec_3_count, addrdec_3_in_out, addrdec_3_reg0, addrdec_3_reg1, addrdec_3_reg2, addrdec_3_reg3,
       addrdec_3_reg4, addrdec_3_reg5, addrdec_3_stack, and_1_out, and_2_out, and_3_out, and_4_out,
       and_5_out, and_6_out, clock_1_out, comparator_1_gt, cond_1_out_4, dec_1_cal, dec_1_def, dec_1_if,
       dec_1_imm1, dec_1_imm2, dec_1_ram, dec_1_regban, or_1_out, or_2_out, or_3_out, or_4_out, or_5_out,
       or_6_out, or_7_out;
  wire [7:0] adder_1_out, alu_1_out, controlled_buffer_1_out, controlled_buffer_2_out,
       controlled_buffer_3_out, counter_1_q, counter_2_q, multiplexer_1_out, rom_2_data, ticker_1_output;
  wire [31:0] rom_1_data;

  Clock clock_1 (.out(clock_1_out));
  or or_1 (or_1_out, or_3_out, addrdec_1_count);
  Ticker ticker_1 (
    .Inc(8'h1), .Output(ticker_1_output), .Replace(or_1_out), .Data(controlled_buffer_3_out),
    .clock(clock_1_out));
  assign controlled_buffer_1_out = addrdec_2_count ? ticker_1_output : 8'bz;  // Controlled_Buffer controlled_buffer_1
  and and_1 (and_1_out, or_2_out, clock_1_out);
  Counter #(.trigger("falling")) counter_1 (.Q(counter_1_q), .clk(and_1_out));  // open: load, D, count, carry, clr
  assign controlled_buffer_2_out = addrdec_3_count ? ticker_1_output : 8'bz;  // Controlled_Buffer controlled_buffer_2
  or or_2 (or_2_out, addrdec_2_in_out, addrdec_3_in_out);
  Adder adder_1 (.a(8'h4), .b(ticker_1_output), .out(adder_1_out));  // open: cin, cout
  or or_3 (or_3_out, dec_1_def, and_4_out);
  ROM #(.dataWidth(32)) rom_1 (.addr(ticker_1_output), .data(rom_1_data));  // open: sel
  ROM rom_2 (.addr(counter_1_q), .data(rom_2_data));  // open: sel
  Dec dec_1 (
    .in_1(rom_1_data[31:24]), .\if (dec_1_if), .imm1(dec_1_imm1), .imm2(dec_1_imm2), .cal(dec_1_cal),
    .def(dec_1_def), .ram(dec_1_ram), .RegBan(dec_1_regban));
  or or_4 (or_4_out, dec_1_def, or_5_out);
  assign controlled_buffer_3_out = or_4_out ? rom_1_data[7:0] : 8'bz;  // Controlled_Buffer controlled_buffer_3
  and and_2 (and_2_out, rom_1_data[27], dec_1_def);
  Stack stack_1 (
    .in_1(and_2_out), .in_3(and_3_out), .in_2(adder_1_out), .out_5(controlled_buffer_3_out),
    .in_4(clock_1_out));
  and and_3 (and_3_out, ~rom_1_data[27], dec_1_def);  // AND_Gate
  AddrDec addrdec_1 (
    .RegBan(or_6_out), .stack(addrdec_1_stack), .Addr(rom_1_data[7:0]), .AddrBan(1'b0),
    .reg0(addrdec_1_reg0), .reg1(addrdec_1_reg1), .reg2(addrdec_1_reg2), .reg3(addrdec_1_reg3),
    .reg4(addrdec_1_reg4), .reg5(addrdec_1_reg5), .count(addrdec_1_count), .in_out(addrdec_1_in_out));  // open: ram
  and and_4 (and_4_out, cond_1_out_4, dec_1_if);
  or or_5 (or_5_out, dec_1_def, dec_1_if);
  or or_6 (or_6_out, dec_1_regban, or_5_out);
  and and_5 (and_5_out, addrdec_1_stack, or_4_out);
  assign controlled_buffer_2_out = dec_1_imm1 ? rom_1_data[23:16] : 8'bz;  // Controlled_Buffer controlled_buffer_4
  AddrDec addrdec_2 (
    .RegBan(1'b0), .stack(addrdec_2_stack), .Addr(rom_1_data[23:16]), .AddrBan(dec_1_imm1),
    .reg0(addrdec_2_reg0), .reg1(addrdec_2_reg1), .reg2(addrdec_2_reg2), .reg3(addrdec_2_reg3),
    .reg4(addrdec_2_reg4), .reg5(addrdec_2_reg5), .count(addrdec_2_count), .in_out(addrdec_2_in_out));  // open: ram
  assign controlled_buffer_2_out = addrdec_2_in_out ? rom_2_data : 8'bz;  // Controlled_Buffer controlled_buffer_5
  assign controlled_buffer_1_out = dec_1_imm2 ? rom_1_data[15:8] : 8'bz;  // Controlled_Buffer controlled_buffer_6
  AddrDec addrdec_3 (
    .RegBan(1'b0), .stack(addrdec_3_stack), .Addr(rom_1_data[15:8]), .AddrBan(dec_1_imm2),
    .reg0(addrdec_3_reg0), .reg1(addrdec_3_reg1), .reg2(addrdec_3_reg2), .reg3(addrdec_3_reg3),
    .reg4(addrdec_3_reg4), .reg5(addrdec_3_reg5), .count(addrdec_3_count), .in_out(addrdec_3_in_out));  // open: ram
  DulRegester dulregester_1 (
    .In(controlled_buffer_3_out), .Ctrl1(addrdec_2_reg0), .Ctrl2(addrdec_3_reg0),
    .Out1(controlled_buffer_2_out), .Out2(controlled_buffer_1_out), .enable(addrdec_1_reg0),
    .clock(clock_1_out));  // open: Out0, clean
  DulRegester dulregester_2 (
    .In(controlled_buffer_3_out), .Ctrl1(addrdec_2_reg1), .Ctrl2(addrdec_3_reg1),
    .Out1(controlled_buffer_2_out), .Out2(controlled_buffer_1_out), .enable(addrdec_1_reg1),
    .clock(clock_1_out));  // open: Out0, clean
  DulRegester dulregester_3 (
    .In(controlled_buffer_3_out), .Ctrl1(addrdec_2_reg2), .Ctrl2(addrdec_3_reg2),
    .Out1(controlled_buffer_2_out), .Out2(controlled_buffer_1_out), .enable(addrdec_1_reg2),
    .clock(clock_1_out));  // open: Out0, clean
  DulRegester dulregester_4 (
    .In(controlled_buffer_3_out), .Ctrl1(addrdec_2_reg3), .Ctrl2(addrdec_3_reg3),
    .Out1(controlled_buffer_2_out), .Out2(controlled_buffer_1_out), .enable(addrdec_1_reg3),
    .clock(clock_1_out));  // open: Out0, clean
  DulRegester dulregester_5 (
    .In(controlled_buffer_3_out), .Ctrl1(addrdec_2_reg4), .Ctrl2(addrdec_3_reg4),
    .Out1(controlled_buffer_2_out), .Out2(controlled_buffer_1_out), .enable(addrdec_1_reg4),
    .clock(clock_1_out));  // open: Out0, clean
  DulRegester dulregester_6 (
    .In(controlled_buffer_3_out), .Ctrl1(addrdec_2_reg5), .Ctrl2(addrdec_3_reg5),
    .Out1(controlled_buffer_2_out), .Out2(controlled_buffer_1_out), .enable(addrdec_1_reg5),
    .clock(clock_1_out));  // open: Out0, clean
  assign controlled_buffer_1_out = addrdec_3_in_out ? rom_2_data : 8'bz;  // Controlled_Buffer controlled_buffer_7
  Cond cond_1 (
    .in_2(controlled_buffer_2_out), .in_3(controlled_buffer_1_out), .out_4(cond_1_out_4),
    .in_1(rom_1_data[26:24]));
  Alu alu_1 (.in1(controlled_buffer_2_out), .in2(controlled_buffer_1_out), .out(alu_1_out), .Opcode(rom_1_data[26:24]));
  assign controlled_buffer_3_out = dec_1_cal ? alu_1_out : 8'bz;  // Controlled_Buffer controlled_buffer_8
  Counter #(.trigger("falling")) counter_2 (.Q(counter_2_q), .clk(and_6_out));  // open: load, D, count, carry, clr
  and and_6 (and_6_out, addrdec_1_in_out, clock_1_out);
  TTY tty_1 (.data(controlled_buffer_3_out[6:0]), .clk(and_6_out), .we(comparator_1_gt));  // open: clr
  Comparator #(.width(7), .mode("unsigned")) comparator_1 (
    .a(controlled_buffer_3_out[6:0]), .b(7'b0101111), .gt(comparator_1_gt));  // open: eq, lt
  or or_7 (or_7_out, addrdec_2_stack, addrdec_3_stack);
  Multiplexer #(.width(8)) multiplexer_1 (
    .in0(controlled_buffer_2_out), .in1(controlled_buffer_1_out), .out(multiplexer_1_out),
    .en(addrdec_3_stack));  // open: sel
  Stack stack_2 (
    .in_1(or_7_out), .in_3(and_5_out), .in_2(multiplexer_1_out), .out_5(controlled_buffer_3_out),
    .in_4(clock_1_out));
  RAM ram_1 (.addr(counter_2_q), .data(controlled_buffer_3_out), .clk(and_6_out), .ld(1'b0));  // open: sel, clr

  // Notes on the sheet:
  //   contents of rom_1 (hex, n*v repeats v):
  //   0 700 700 80000007 0 0 7 0 7 0 7 a4000000
  //   contents of rom_2 (hex, n*v repeats v):
  //   1 2 3 4 5 6 7 8 9 a b c d e f 10
endmodule

module DulRegester (
  input  enable,
  input  [7:0] In,
  input  Ctrl1,
  input  Ctrl2,
  input  clock,
  input  clean,
  output [7:0] Out0,
  output [7:0] Out1,
  output [7:0] Out2
);

  Register #(.trigger("falling")) register_1 (.D(In), .en(enable), .Q(Out0), .clk(clock), .clr(clean));
  assign Out1 = Ctrl1 ? Out0 : 8'bz;  // Controlled_Buffer controlled_buffer_1
  assign Out2 = Ctrl2 ? Out0 : 8'bz;  // Controlled_Buffer controlled_buffer_2
endmodule

module Dec (
  input  [7:0] in_1,
  output def,
  output \if ,
  output imm1,
  output imm2,
  output cal,
  output ram,
  output RegBan
);

  wire not_1_out, not_2_out, not_3_out, not_4_out, not_5_out;

  and and_1 (def, in_1[5], in_1[4]);
  not not_1 (not_1_out, in_1[4]);
  not not_2 (not_2_out, in_1[3]);
  not not_3 (not_3_out, in_1[4]);
  not not_4 (not_4_out, in_1[5]);
  and and_2 (ram, not_4_out, not_3_out, in_1[3]);
  not not_5 (not_5_out, in_1[2]);
  and and_3 (RegBan, ram, not_5_out);
  and and_4 (\if , in_1[5], not_1_out, not_2_out);
  nor nor_1 (cal, in_1[3], in_1[5]);

  assign imm1 = in_1[6];
  assign imm2 = in_1[7];
endmodule

module AddrDec (
  input  [7:0] Addr,
  input  AddrBan,
  input  RegBan,
  output stack,
  output count,
  output ram,
  output reg0,
  output reg1,
  output reg2,
  output reg3,
  output reg4,
  output reg5,
  output in_out
);

  wire decoder_1_out0, decoder_1_out1, decoder_1_out2, decoder_1_out3, decoder_1_out4, decoder_1_out5,
       decoder_1_out6, decoder_1_out7, nor_1_out;

  and and_1 (count, nor_1_out, decoder_1_out6);
  and and_2 (stack, Addr[6], ~AddrBan);  // AND_Gate
  and and_3 (ram, ~AddrBan, Addr[7]);  // AND_Gate
  nor nor_1 (nor_1_out, ram, stack, AddrBan, RegBan);
  and and_4 (reg2, nor_1_out, decoder_1_out2);
  and and_5 (reg1, nor_1_out, decoder_1_out1);
  and and_6 (reg0, nor_1_out, decoder_1_out0);
  Decoder #(.select(3)) decoder_1 (
    .out0(decoder_1_out0), .out1(decoder_1_out1), .out2(decoder_1_out2), .out3(decoder_1_out3),
    .out4(decoder_1_out4), .out5(decoder_1_out5), .out6(decoder_1_out6), .out7(decoder_1_out7),
    .sel(Addr[2:0]));  // open: en
  and and_7 (reg5, nor_1_out, decoder_1_out5);
  and and_8 (reg3, nor_1_out, decoder_1_out3);
  and and_9 (reg4, nor_1_out, decoder_1_out4);
  and and_10 (in_out, nor_1_out, decoder_1_out7);
endmodule

module Alu (
  input  [2:0] Opcode,
  input  [7:0] in1,
  input  [7:0] in2,
  output [7:0] out
);

  wire [7:0] adder_1_out, and_1_out, not_1_out, or_1_out, shifter_1_out, shifter_2_out, subtractor_1_out,
       xor_1_out;

  Adder adder_1 (.a(in1), .b(in2), .out(adder_1_out));  // open: cin, cout
  Subtractor subtractor_1 (.a(in1), .b(in2), .out(subtractor_1_out));  // open: bin, bout
  assign and_1_out = in1 & in2;  // AND_Gate and_1, 8 bits wide
  assign or_1_out = in1 | in2;  // OR_Gate or_1, 8 bits wide
  assign not_1_out = ~in1;  // NOT_Gate not_1, 8 bits wide
  assign xor_1_out = in2 ^ in1;  // XOR_Gate xor_1, 8 bits wide
  Shifter shifter_1 (.in(in1), .\dist (in2[2:0]), .out(shifter_1_out));
  Shifter #(.shift("lr")) shifter_2 (.in(in1), .\dist (in2[2:0]), .out(shifter_2_out));
  Multiplexer #(.select(3), .width(8)) multiplexer_1 (
    .in0(adder_1_out), .in1(subtractor_1_out), .in2(and_1_out), .in3(or_1_out), .in4(not_1_out),
    .in5(xor_1_out), .in6(shifter_1_out), .in7(shifter_2_out), .out(out), .sel(Opcode));  // open: en
endmodule

module Cond (
  input  [2:0] in_1,
  input  [7:0] in_2,
  input  [7:0] in_3,
  output out_4
);

  wire and_1_out, and_2_out, and_3_out, comparator_1_eq, comparator_1_gt, comparator_1_lt, nor_1_out;

  Comparator #(.mode("unsigned")) comparator_1 (
    .a(in_2), .b(in_3), .gt(comparator_1_gt), .eq(comparator_1_eq), .lt(comparator_1_lt));
  and and_1 (and_1_out, in_1[2], comparator_1_gt);
  and and_2 (and_2_out, in_1[0], comparator_1_eq);
  and and_3 (and_3_out, comparator_1_lt, in_1[1]);
  nor nor_1 (nor_1_out, in_1[0], in_1[1], in_1[2], comparator_1_eq);
  or or_1 (out_4, nor_1_out, and_1_out, and_2_out, and_3_out);
endmodule

module Ticker (
  input  Replace,
  input  [7:0] Inc,
  input  [7:0] Data,
  input  clock,
  output [7:0] Output
);

  wire [7:0] adder_1_out, multiplexer_1_out;

  Adder adder_1 (.a(Output), .b(Inc), .out(adder_1_out));  // open: cin, cout
  Multiplexer #(.width(8)) multiplexer_1 (
    .in0(adder_1_out), .in1(Data), .out(multiplexer_1_out), .sel(Replace));  // open: en
  Register #(.trigger("falling")) register_1 (.D(multiplexer_1_out), .en(1'b1), .Q(Output), .clk(clock));  // open: clr
endmodule

module Stack (
  input  in_1,
  input  [7:0] in_2,
  input  in_3,
  input  in_4,
  output [7:0] out_5
);
endmodule
